// Logisim project BigASM.circ as structural Verilog
module BOARD_BIG_ASM (
  output out_1
);

  wire button_1_out, CLK, CLR, d_ff_1_q, not_1_out, Write, Write_ASCII;
  wire [6:0] ASCII;
  wire [7:0] counter_1_q;
  wire [23:0] Dir_INPUT, Dir_MEMORY;
  wire [31:0] INPUT, MEMORY_IN, MEMORY_OUT;

  Button button_1 (.out(button_1_out));
  Clock clock_1 (.out(CLK));
  D_Flip_Flop d_ff_1 (.clk(CLK), .D(1'b1), .Q(d_ff_1_q), .reset(button_1_out));  // open: Qn, preset, en
  D_Flip_Flop d_ff_2 (.clk(CLK), .D(d_ff_1_q), .Qn(CLR), .reset(button_1_out));  // open: Q, preset, en
  BIG_ASM big_asm_1 (
    .DATA_INPUT(INPUT), .MEMORY_IN(MEMORY_OUT), .CLK(CLK), .CLR(CLR), .DIR_INPUT(Dir_INPUT),
    .MEMORY_OUT(MEMORY_IN), .DIR_MEMORY(Dir_MEMORY), .Write_OUTPUT(Write), .ASCII(ASCII),
    .Write_ASCII(Write_ASCII), .END(out_1));
  MEMORY memory_1 (.DIR(Dir_MEMORY), .DATA_IN(MEMORY_IN), .WRITE(Write), .CLK(CLK), .CLR(CLR), .DATA_OUT(MEMORY_OUT));
  INPUT input_1 (.DIR(Dir_INPUT), .CLK(CLK), .DATA_OUT(INPUT));
  Counter counter_1 (.load(1'b0), .count(not_1_out), .Q(counter_1_q), .clk(CLK), .clr(CLR));  // open: D, carry
  not not_1 (not_1_out, out_1);
  // Probe on counter_1_q
  TTY #(.rows(32), .cols(60)) tty_1 (.data(ASCII), .clk(CLK), .we(Write_ASCII), .clr(CLR));

  // Other names for the same wires on the sheet: END = out_1

  // Notes on the sheet:
  //   COUNTER
  //   BOARD
endmodule

module INPUT (
  input  [23:0] DIR,
  input  CLK,
  output [31:0] DATA_OUT
);

  RAM #(.addrWidth(24), .dataWidth(32)) ram_1 (.addr(DIR), .data(DATA_OUT), .clk(CLK), .ld(1'b1));  // open: sel, clr
endmodule

module MEMORY (
  input  [23:0] DIR,
  input  [31:0] DATA_IN,
  input  WRITE,
  input  CLK,
  input  CLR,
  output [31:0] DATA_OUT
);

  wire not_1_out;

  not not_1 (not_1_out, WRITE);
  RAM #(.addrWidth(24), .dataWidth(32), .bus("separate")) ram_1 (
    .addr(DIR), .din(DATA_IN), .data(DATA_OUT), .clk(CLK), .ld(not_1_out), .clr(CLR));  // open: str, sel
endmodule

module BIG_ASM (
  input  [31:0] DATA_INPUT,
  input  [31:0] MEMORY_IN,
  input  CLK,
  input  CLR,
  output [23:0] DIR_INPUT,
  output [31:0] MEMORY_OUT,
  output [23:0] DIR_MEMORY,
  output Write_OUTPUT,
  output [6:0] ASCII,
  output Write_ASCII,
  output END
);

  wire A_B, and_1_out, and_2_out, button_1_out, control_unit_1_sout0, LA, LB, LOp, LP1, LP2, LT1, LT2,
       not_1_out, not_2_out, P1_T1, P2_T2, SdIR, SOp0, SOp1, SP2, sPrinter, STOP, T1_T2, T1_T2_t;
  wire [31:0] OUT;

  Button button_1 (.out(button_1_out));
  Control_Unit control_unit_1 (
    .START(button_1_out), .CLK(CLK), .CLR(CLR), .A_B(A_B), .T1_T2(T1_T2_t), .P1_T1(P1_T1), .P2_T2(P2_T2),
    .SOut0(control_unit_1_sout0), .SOut1(control_unit_1_sout0), .SOut2(control_unit_1_sout0), .SOp0(SOp0),
    .SOp1(SOp1), .SP2(SP2), .END(sPrinter), .out_16(LA), .out_17(LB), .out_18(LP1), .out_19(LP2),
    .out_20(LT1), .out_21(LT2), .out_22(LOp), .SDIR(SdIR), .T1_T2_2(T1_T2));
  Data_Path data_path_1 (
    .Sout0(control_unit_1_sout0), .Sout1(control_unit_1_sout0), .Sout2(control_unit_1_sout0),
    .DATA_IN(DATA_INPUT), .CLK(CLK), .CLR(CLR), .LA(LA), .LB(LB), .LP1(LP1), .LP2(LP2), .LT1(LT1), .LT2(LT2),
    .LOp(LOp), .DATA_OUT(OUT), .T1_T2(T1_T2_t), .A_B(A_B), .P1_T1(P1_T1), .P1_T2(P2_T2), .SOp0(SOp0),
    .SOp1(SOp1), .SP2(SP2), .DIR(DIR_INPUT), .SDIR(SdIR), .T1_T2_2(T1_T2));
  not not_1 (not_1_out, STOP);
  and and_1 (and_1_out, sPrinter, not_1_out);
  PRINT_UDEC print_udec_1 (
    .num(OUT), .start(and_1_out), .CLK(CLK), .RST(CLR), .ASCII(ASCII), .Write_ASCII(Write_ASCII), .\end (END));
  Counter #(.width(1), .max('h1)) counter_1 (
    .count(and_2_out), .carry(STOP), .clk(CLK), .clr(CLR));  // open: load, D, Q
  and and_2 (and_2_out, END, not_2_out);
  not not_2 (not_2_out, STOP);

  // Other names for the same wires on the sheet: DI[31:0] = DATA_INPUT; DIR[23:0] = DIR_INPUT; WASCII = Write_ASCII
endmodule

module PRINT_UDEC (
  input  [31:0] num,
  input  start,
  input  CLK,
  input  RST,
  output [6:0] ASCII,
  output Write_ASCII,
  output \end 
);

  wire _0_c, _0_n, demultiplexer_1_out0, demultiplexer_2_out0, demultiplexer_2_out1, demultiplexer_3_out0,
       demultiplexer_3_out1, IDLE_2_q, IDLE_3_q, IDLE_4_q, IDLE_q, Lc, Lc_0, Ln, Ln_0, or_1_out;
  wire [23:0] bit_extender_1_out;
  wire [31:0] c, c___1, c___1_t, divider_1_rem, memory_1_data_out, multiplexer_1_out, multiplexer_2_out,
       multiplexer_3_out, n, n___10, n___10___48;

  Multiplexer #(.width(32), .enable("false")) multiplexer_1 (
    .in0(num), .in1(n___10), .out(multiplexer_1_out), .sel(Lc_0));
  Divider #(.width(32)) divider_1 (.a(n), .b(32'ha), .out(n___10), .rem(divider_1_rem));  // open: upper
  Adder #(.width(32)) adder_1 (.a(divider_1_rem), .b(32'h30), .out(n___10___48));  // open: cin, cout
  or or_1 (or_1_out, demultiplexer_1_out0, \end );
  Register #(.width(32)) u_n (.D(multiplexer_1_out), .en(Ln), .Q(n), .clk(CLK), .clr(RST));
  D_Flip_Flop IDLE (.clk(CLK), .D(or_1_out), .Q(IDLE_q), .preset(RST));  // open: Qn, en, reset
  Demultiplexer #(.enable("false")) demultiplexer_1 (
    .out0(demultiplexer_1_out0), .out1(Ln_0), .in(IDLE_q), .sel(start));
  or or_2 (Write_ASCII, demultiplexer_3_out0, demultiplexer_2_out1);
  Multiplexer #(.width(32), .enable("false")) multiplexer_2 (
    .in0(c___1), .in1(c___1_t), .out(multiplexer_2_out), .sel(Write_ASCII));
  Adder #(.width(32)) adder_2 (.a(c), .b(32'h1), .out(c___1));  // open: cin, cout
  Subtractor #(.width(32)) subtractor_1 (.a(c), .b(32'h1), .out(c___1_t));  // open: bin, bout
  D_Flip_Flop IDLE_2 (.clk(CLK), .D(Ln_0), .Q(IDLE_2_q), .reset(RST));  // open: Qn, preset, en
  Register #(.width(32)) u_c (.D(multiplexer_2_out), .en(Lc), .Q(c), .clk(CLK), .clr(RST));
  or or_3 (Lc_0, IDLE_2_q, demultiplexer_3_out1);
  Multiplexer #(.width(32), .enable("false")) multiplexer_3 (
    .in0(c), .in1(c___1_t), .out(multiplexer_3_out), .sel(Write_ASCII));
  Comparator #(.width(32), .mode("unsigned")) comparator_1 (.a({32{1'b0}}), .b(n), .lt(_0_n));  // open: gt, eq
  Comparator #(.width(32), .mode("unsigned")) comparator_2 (.a({32{1'b0}}), .b(c), .lt(_0_c));  // open: gt, eq
  D_Flip_Flop IDLE_3 (.clk(CLK), .D(Write_ASCII), .Q(IDLE_3_q), .reset(RST));  // open: Qn, preset, en
  Demultiplexer #(.enable("false")) demultiplexer_2 (
    .out0(demultiplexer_2_out0), .out1(demultiplexer_2_out1), .in(IDLE_3_q), .sel(_0_c));
  Bit_Extender #(.in_width(32), .out_width(24)) bit_extender_1 (.in(multiplexer_3_out), .out(bit_extender_1_out));
  D_Flip_Flop IDLE_4 (.clk(CLK), .D(Lc_0), .Q(IDLE_4_q), .reset(RST));  // open: Qn, preset, en
  or or_4 (Lc, Lc_0, Write_ASCII);
  or or_5 (Ln, Ln_0, Lc_0);
  Demultiplexer #(.enable("false")) demultiplexer_3 (
    .out0(demultiplexer_3_out0), .out1(demultiplexer_3_out1), .in(IDLE_4_q), .sel(_0_n));
  D_Flip_Flop IDLE_5 (.clk(CLK), .D(demultiplexer_2_out0), .Q(\end ), .reset(RST));  // open: Qn, preset, en
  MEMORY memory_1 (
    .DIR(bit_extender_1_out), .DATA_IN(n___10___48), .WRITE(Lc_0), .CLK(CLK), .CLR(RST),
    .DATA_OUT(memory_1_data_out));
  Bit_Extender #(.in_width(32), .out_width(7)) bit_extender_2 (.in(memory_1_data_out), .out(ASCII));

  // Other names for the same wires on the sheet: Lc_1 = Write_ASCII; Sc = Write_ASCII; Ln_1 = Lc_0; Sn = Lc_0;
  //   Write = Lc_0
endmodule

module PRINT_DEC (
  input  [31:0] num,
  input  start,
  input  CLK,
  input  RST,
  output [6:0] ASCII,
  output Write_ASCII,
  output END
);

  wire demultiplexer_1_out0, demultiplexer_1_out1, demultiplexer_2_out0, demultiplexer_3_out0, end_t,
       IDLE_3_q, IDLE_q, or_1_out, or_2_out, or_3_out, S_ASCII, startUDEC, Write_ASCII_1;
  wire [6:0] ASCII_t;
  wire [31:0] multiplexer_1_out, negator_1_out;

  or or_1 (or_1_out, demultiplexer_1_out0, END);
  Negator #(.width(32)) negator_1 (.in(num), .out(negator_1_out));
  D_Flip_Flop IDLE (.clk(CLK), .D(or_1_out), .Q(IDLE_q), .preset(RST));  // open: Qn, en, reset
  Demultiplexer #(.enable("false")) demultiplexer_1 (
    .out0(demultiplexer_1_out0), .out1(demultiplexer_1_out1), .in(IDLE_q), .sel(start));
  Multiplexer #(.width(32), .enable("false")) multiplexer_1 (
    .in0(num), .in1(negator_1_out), .out(multiplexer_1_out), .sel(num[31]));
  Demultiplexer #(.enable("false")) demultiplexer_2 (
    .out0(demultiplexer_2_out0), .out1(S_ASCII), .in(demultiplexer_1_out1), .sel(num[31]));
  or or_2 (or_2_out, demultiplexer_2_out0, S_ASCII);
  D_Flip_Flop IDLE_2 (.clk(CLK), .D(or_2_out), .Q(startUDEC), .reset(RST));  // open: Qn, preset, en
  PRINT_UDEC print_udec_1 (
    .num(multiplexer_1_out), .start(startUDEC), .CLK(CLK), .RST(RST), .ASCII(ASCII_t),
    .Write_ASCII(Write_ASCII_1), .\end (end_t));
  D_Flip_Flop IDLE_3 (.clk(CLK), .D(or_3_out), .Q(IDLE_3_q), .reset(RST));  // open: Qn, preset, en
  or or_3 (or_3_out, startUDEC, demultiplexer_3_out0);
  Demultiplexer #(.enable("false")) demultiplexer_3 (
    .out0(demultiplexer_3_out0), .out1(END), .in(IDLE_3_q), .sel(end_t));
  Multiplexer #(.width(7), .enable("false")) multiplexer_2 (
    .in0(ASCII_t), .in1(7'b0101101), .out(ASCII), .sel(S_ASCII));
  or or_4 (Write_ASCII, S_ASCII, Write_ASCII_1);

  // Other names for the same wires on the sheet: sign = num[31]; Write_ASCII_0 = S_ASCII
endmodule

module TEST_PRINT (
  input  [31:0] in_1,
  output out_2
);

  wire button_1_out, button_2_out, CLK, CLR, d_ff_1_q, Write_ASCII;
  wire [6:0] ASCII;

  Button button_1 (.out(button_1_out));
  Clock clock_1 (.out(CLK));
  D_Flip_Flop d_ff_1 (.clk(CLK), .D(1'b1), .Q(d_ff_1_q), .reset(button_1_out));  // open: Qn, preset, en
  D_Flip_Flop d_ff_2 (.clk(CLK), .D(d_ff_1_q), .Qn(CLR), .reset(button_1_out));  // open: Q, preset, en
  Button button_2 (.out(button_2_out));
  PRINT_UDEC print_udec_1 ();  // open: num, start, CLK, RST, ASCII, Write_ASCII, end
  PRINT_DEC print_dec_1 (
    .num(in_1), .start(button_2_out), .CLK(CLK), .RST(CLR), .ASCII(ASCII), .Write_ASCII(Write_ASCII),
    .END(out_2));
  TTY #(.rows(32), .cols(60)) tty_1 (.data(ASCII), .clk(CLK), .we(Write_ASCII), .clr(CLR));
endmodule

module Control_Unit (
  input  START,
  input  CLK,
  input  CLR,
  input  A_B,
  input  T1_T2,
  input  P1_T1,
  input  P2_T2,
  input  T1_T2_2,
  output SOut0,
  output SOut1,
  output SOut2,
  output SOp0,
  output SOp1,
  output SP2,
  output END,
  output out_16,
  output out_17,
  output out_18,
  output out_19,
  output out_20,
  output out_21,
  output out_22,
  output SDIR
);

  wire B_q, CONTINUE, CONTINUE_1, CONTINUE_2, demultiplexer_1_out0, demultiplexer_1_out1,
       demultiplexer_2_out0, demultiplexer_6_out0, END_1, END_2, FINISH, IDLE_q, LP2_2, or_1_out, or_5_out,
       or_6_out, or_7_out, STARTER, W_COND, WHILE_q;

  or or_1 (or_1_out, demultiplexer_1_out0, STARTER);
  D_Flip_Flop IDLE (.clk(CLK), .D(or_1_out), .Q(IDLE_q), .preset(CLR));  // open: Qn, en, reset
  D_Flip_Flop A (.clk(CLK), .D(out_16), .Q(out_17), .reset(CLR));  // open: Qn, preset, en
  Demultiplexer demultiplexer_1 (
    .out0(demultiplexer_1_out0), .out1(demultiplexer_1_out1), .in(IDLE_q), .sel(START));  // open: en
  Demultiplexer demultiplexer_2 (.out0(demultiplexer_2_out0), .out1(END_2), .in(FINISH), .sel(T1_T2_2));  // open: en
  or or_2 (out_19, SP2, LP2_2, CONTINUE_2, CONTINUE_1);
  D_Flip_Flop B (.clk(CLK), .D(out_17), .Q(B_q), .reset(CLR));  // open: Qn, preset, en
  Demultiplexer demultiplexer_3 (.out0(CONTINUE_1), .out1(CONTINUE_2), .in(B_q), .sel(A_B));  // open: en
  D_Flip_Flop LOAD1 (.clk(CLK), .D(demultiplexer_1_out1), .Q(out_20), .reset(CLR));  // open: Qn, preset, en
  Demultiplexer demultiplexer_4 (.out0(SOp1), .out1(END_1), .in(demultiplexer_2_out0), .sel(T1_T2));  // open: en
  D_Flip_Flop LOAD2 (.clk(CLK), .D(out_20), .Q(SP2), .reset(CLR));  // open: Qn, preset, en
  or or_3 (out_18, SP2, CONTINUE_2, CONTINUE_1);
  D_Flip_Flop LOAD3 (.clk(CLK), .D(SP2), .Q(out_21), .reset(CLR));  // open: Qn, preset, en
  and u_W_COND (W_COND, P1_T1, P2_T2);
  or or_4 (out_22, CONTINUE_1, SOp1, END_1);
  D_Flip_Flop TOSTART (.clk(CLK), .D(out_21), .Q(LP2_2), .reset(CLR));  // open: Qn, preset, en
  or or_5 (or_5_out, SOp1, END_1, END_2);
  or or_6 (or_6_out, CONTINUE, LP2_2);
  or or_7 (or_7_out, demultiplexer_6_out0, or_5_out);
  or or_8 (SOp0, END_1, SOp1);
  or or_9 (SDIR, out_21, out_17);
  D_Flip_Flop WHILE (.clk(CLK), .D(or_6_out), .Q(WHILE_q), .reset(CLR));  // open: Qn, preset, en
  Demultiplexer demultiplexer_5 (.out0(FINISH), .out1(out_16), .in(WHILE_q), .sel(W_COND));  // open: en
  Demultiplexer demultiplexer_6 (.out0(demultiplexer_6_out0), .out1(STARTER), .in(END), .sel(START));  // open: en
  D_Flip_Flop IDLE_2 (.clk(CLK), .D(or_7_out), .Q(END), .reset(CLR));  // open: Qn, preset, en
  or or_10 (CONTINUE, CONTINUE_1, CONTINUE_2);

  // Other names for the same wires on the sheet: LA = out_16; LOOP = out_16; LOp = out_22; LP1 = out_18; LP2 = out_19;
  //   LP1_1 = SP2; LP2_1 = SP2; IF = CONTINUE_2; LP1_2 = CONTINUE_2; LP2_3 = CONTINUE_2; ELSE = CONTINUE_1;
  //   LOp_1 = CONTINUE_1; LP1_3 = CONTINUE_1; LP2_4 = CONTINUE_1; LT1 = out_20; P1_T2 = P2_T2; LT2 = out_21;
  //   SDIR_1 = out_21; LB = out_17; SDIR_2 = out_17; END_0 = SOp1; LOp_2 = SOp1; SOp0_1 = SOp1; LOp_3 = END_1;
  //   SOp0_2 = END_1; T1_T2_t = T1_T2_2
endmodule

module Data_Path (
  input  Sout0,
  input  Sout1,
  input  Sout2,
  input  [31:0] DATA_IN,
  input  CLK,
  input  CLR,
  input  LA,
  input  LB,
  input  LP1,
  input  LP2,
  input  LT1,
  input  LT2,
  input  LOp,
  input  SDIR,
  input  SOp0,
  input  SOp1,
  input  SP2,
  output [31:0] DATA_OUT,
  output [23:0] DIR,
  output T1_T2,
  output T1_T2_2,
  output A_B,
  output P1_T1,
  output P1_T2
);

  wire comparator_3_eq, comparator_3_lt, comparator_4_eq, comparator_4_lt;
  wire [23:0] DP1, DP2;
  wire [31:0] A, B, multiplexer_2_out, multiplexer_3_out, Op__1, Op____T1___P1, Op____T2___P1, OUT, P1_1,
       P1_1_t, P2_1, subtractor_2_out, subtractor_3_out, T1, T1_1, T2;
  wire [31:24] P1, P2;

  Register #(.width(32)) u_A (.D(DATA_IN), .en(LA), .Q(A), .clk(CLK), .clr(CLR));
  Register #(.width(32)) u_T1 (.D(DATA_IN), .en(LT1), .Q(T1), .clk(CLK), .clr(CLR));
  Multiplexer #(.select(3), .width(32)) multiplexer_1 (
    .in0(A), .in1(B), .in2({P1, DP1}), .in3({P2, DP2}), .in4(T1), .in5(T2), .in6(DATA_OUT), .out(OUT),
    .sel({Sout2, Sout1, Sout0}));  // open: in7, en
  Register #(.width(32)) u_B (.D(DATA_IN), .en(LB), .Q(B), .clk(CLK), .clr(CLR));
  Register #(.width(32)) u_T2 (.D(DATA_IN), .en(LT2), .Q(T2), .clk(CLK), .clr(CLR));
  Subtractor #(.width(32)) subtractor_1 (.a({P1, DP1}), .b(32'h1), .out(P1_1_t));  // open: bin, bout
  Register #(.width(32)) u_P1 (.D(P1_1), .en(LP1), .Q({P1, DP1}), .clk(CLK), .clr(CLR));
  Subtractor #(.width(32)) subtractor_2 (.a(T2), .b(P1_1_t), .out(subtractor_2_out));  // open: bin, bout
  Subtractor #(.width(32)) subtractor_3 (.a(T1), .b(P1_1_t), .out(subtractor_3_out));  // open: bin, bout
  Multiplexer #(.select(2), .width(32)) multiplexer_2 (
    .in0(Op__1), .in1(Op____T1___P1), .in3(Op____T2___P1), .out(multiplexer_2_out), .sel({SOp1, SOp0}));  // open: in2, en
  Multiplexer #(.width(32)) multiplexer_3 (.in0(P2_1), .in1(T1_1), .out(multiplexer_3_out), .sel(SP2));  // open: en
  Adder #(.width(32)) adder_1 (.a(DATA_OUT), .b(subtractor_2_out), .out(Op____T2___P1));  // open: cin, cout
  Adder #(.width(32)) adder_2 (.a(DATA_OUT), .b(subtractor_3_out), .out(Op____T1___P1));  // open: cin, cout
  Register #(.width(32)) OP (.D(multiplexer_2_out), .en(LOp), .Q(DATA_OUT), .clk(CLK), .clr(CLR));
  Register #(.width(32)) u_P2 (.D(multiplexer_3_out), .en(LP2), .Q({P2, DP2}), .clk(CLK), .clr(CLR));
  Adder #(.width(32)) adder_3 (.a(DATA_OUT), .b(32'h1), .out(Op__1));  // open: cin, cout
  Multiplexer #(.width(24)) multiplexer_4 (.in0(DP1), .in1(DP2), .out(DIR), .sel(SDIR));  // open: en
  Adder #(.width(32)) adder_4 (.a(T1), .b(32'h1), .out(T1_1));  // open: cin, cout
  Adder #(.width(32)) adder_5 (.a({P2, DP2}), .b(32'h1), .out(P2_1));  // open: cin, cout
  Adder #(.width(32)) adder_6 (.a({P1, DP1}), .b(32'h1), .out(P1_1));  // open: cin, cout
  Comparator #(.width(32), .mode("unsigned")) comparator_1 (.a(T1), .b(T2), .gt(T1_T2), .eq(T1_T2_2));  // open: lt
  Comparator #(.width(32), .mode("unsigned")) comparator_2 (.a(A), .b(B), .eq(A_B));  // open: gt, lt
  Comparator #(.width(32), .mode("unsigned")) comparator_3 (
    .a({P1, DP1}), .b(T1), .eq(comparator_3_eq), .lt(comparator_3_lt));  // open: gt
  Comparator #(.width(32), .mode("unsigned")) comparator_4 (
    .a({P1, DP1}), .b(T2), .eq(comparator_4_eq), .lt(comparator_4_lt));  // open: gt
  or or_1 (P1_T1, comparator_3_eq, comparator_3_lt);
  or or_2 (P1_T2, comparator_4_eq, comparator_4_lt);

  // Other names for the same wires on the sheet: DI[31:0] = DATA_IN; P1[23:0] = DP1; P2[23:0] = DP2;
  //   OP[31:0] = DATA_OUT
endmodule
