// Logisim project BigASM.circ as structural Verilog
module BOARD_BIG_ASM (
  output out_1
);

  wire button_1_out, CLK, CLR, d_ff_1_q, not_1_out, Write, Write_ASCII;
  wire [6:0] ASCII;
  wire [7:0] counter_1_q;
  wire [23:0] Dir_INPUT, Dir_MEMORY;
  wire [31:0] INPUT, MEMORY_IN, MEMORY_OUT;

  Button button_1 (.out(button_1_out));
  Clock clock_1 (.out(CLK));
  D_Flip_Flop d_ff_1 (.clk(CLK), .D(1'b1), .Q(d_ff_1_q), .reset(button_1_out));  // open: Qn, preset, en
  D_Flip_Flop d_ff_2 (.clk(CLK), .D(d_ff_1_q), .Qn(CLR), .reset(button_1_out));  // open: Q, preset, en
  BIG_ASM big_asm_1 (
    .DATA_INPUT(INPUT), .MEMORY_IN(MEMORY_OUT), .CLK(CLK), .CLR(CLR), .DIR_INPUT(Dir_INPUT),
    .MEMORY_OUT(MEMORY_IN), .DIR_MEMORY(Dir_MEMORY), .Write_OUTPUT(Write), .ASCII(ASCII),
    .Write_ASCII(Write_ASCII), .END(out_1));
  MEMORY memory_1 (.DIR(Dir_MEMORY), .DATA_IN(MEMORY_IN), .WRITE(Write), .CLK(CLK), .CLR(CLR), .DATA_OUT(MEMORY_OUT));
  INPUT input_1 (.DIR(Dir_INPUT), .CLK(CLK), .DATA_OUT(INPUT));
  Counter counter_1 (.load(1'b0), .count(not_1_out), .Q(counter_1_q), .clk(CLK), .clr(CLR));  // open: D, carry
  not not_1 (not_1_out, out_1);
  // Probe on counter_1_q
  TTY #(.rows(32), .cols(60)) tty_1 (.data(ASCII), .clk(CLK), .we(Write_ASCII), .clr(CLR));

  // Other names for the same wires on the sheet: END = out_1

  // Notes on the sheet:
  //   COUNTER
  //   BOARD
endmodule

module INPUT (
  input  [23:0] DIR,
  input  CLK,
  output [31:0] DATA_OUT
);

  RAM #(.addrWidth(24), .dataWidth(32)) ram_1 (.addr(DIR), .data(DATA_OUT), .clk(CLK), .ld(1'b1));  // open: sel, clr
endmodule

module MEMORY (
  input  [23:0] DIR,
  input  [31:0] DATA_IN,
  input  WRITE,
  input  CLK,
  input  CLR,
  output [31:0] DATA_OUT
);

  wire not_1_out;

  not not_1 (not_1_out, WRITE);
  RAM #(.addrWidth(24), .dataWidth(32), .bus("separate")) ram_1 (
    .addr(DIR), .din(DATA_IN), .data(DATA_OUT), .str(WRITE), .clk(CLK), .ld(not_1_out), .clr(CLR));  // open: sel
endmodule

module BIG_ASM (
  input  [31:0] DATA_INPUT,
  input  [31:0] MEMORY_IN,
  input  CLK,
  input  CLR,
  output [23:0] DIR_INPUT,
  output [31:0] MEMORY_OUT,
  output [23:0] DIR_MEMORY,
  output Write_OUTPUT,
  output [6:0] ASCII,
  output Write_ASCII,
  output END
);

  Counter #(.width(24), .max('hffffff)) counter_1 (
    .load(END), .D(24'hffff98), .clk(CLK));  // open: count, Q, carry, clr
  cpu cpu_1 (
    .clk(CLK), .ram_data(MEMORY_IN), .ram_addr(DIR_MEMORY), .write_in_ram(MEMORY_OUT),
    .ram_write(Write_OUTPUT), .data(DATA_INPUT), .\end (END), .input_addr(DIR_INPUT), .clr(CLR));

  assign Write_ASCII = END;
endmodule

module PRINT_UDEC (
  input  [31:0] num,
  input  start,
  input  CLK,
  input  RST,
  output [6:0] ASCII,
  output Write_ASCII,
  output \end 
);

  wire _0_c, _0_n, demultiplexer_1_out0, demultiplexer_2_out0, demultiplexer_2_out1, demultiplexer_3_out0,
       demultiplexer_3_out1, IDLE_2_q, IDLE_3_q, IDLE_4_q, IDLE_q, Lc, Lc_0, Ln, Ln_0, or_1_out;
  wire [23:0] bit_extender_1_out;
  wire [31:0] c, c___1, c___1_t, divider_1_rem, memory_1_data_out, multiplexer_1_out, multiplexer_2_out,
       multiplexer_3_out, n, n___10, n___10___48;

  Multiplexer #(.width(32), .enable("false")) multiplexer_1 (
    .in0(num), .in1(n___10), .out(multiplexer_1_out), .sel(Lc_0));
  Divider #(.width(32)) divider_1 (.a(n), .b(32'ha), .out(n___10), .rem(divider_1_rem));  // open: upper
  Adder #(.width(32)) adder_1 (.a(divider_1_rem), .b(32'h30), .out(n___10___48));  // open: cin, cout
  or or_1 (or_1_out, demultiplexer_1_out0, \end );
  Register #(.width(32)) u_n (.D(multiplexer_1_out), .en(Ln), .Q(n), .clk(CLK), .clr(RST));
  D_Flip_Flop IDLE (.clk(CLK), .D(or_1_out), .Q(IDLE_q), .preset(RST));  // open: Qn, en, reset
  Demultiplexer #(.enable("false")) demultiplexer_1 (
    .out0(demultiplexer_1_out0), .out1(Ln_0), .in(IDLE_q), .sel(start));
  or or_2 (Write_ASCII, demultiplexer_3_out0, demultiplexer_2_out1);
  Multiplexer #(.width(32), .enable("false")) multiplexer_2 (
    .in0(c___1), .in1(c___1_t), .out(multiplexer_2_out), .sel(Write_ASCII));
  Adder #(.width(32)) adder_2 (.a(c), .b(32'h1), .out(c___1));  // open: cin, cout
  Subtractor #(.width(32)) subtractor_1 (.a(c), .b(32'h1), .out(c___1_t));  // open: bin, bout
  D_Flip_Flop IDLE_2 (.clk(CLK), .D(Ln_0), .Q(IDLE_2_q), .reset(RST));  // open: Qn, preset, en
  Register #(.width(32)) u_c (.D(multiplexer_2_out), .en(Lc), .Q(c), .clk(CLK), .clr(RST));
  or or_3 (Lc_0, IDLE_2_q, demultiplexer_3_out1);
  Multiplexer #(.width(32), .enable("false")) multiplexer_3 (
    .in0(c), .in1(c___1_t), .out(multiplexer_3_out), .sel(Write_ASCII));
  Comparator #(.width(32), .mode("unsigned")) comparator_1 (.a({32{1'b0}}), .b(n), .lt(_0_n));  // open: gt, eq
  Comparator #(.width(32), .mode("unsigned")) comparator_2 (.a({32{1'b0}}), .b(c), .lt(_0_c));  // open: gt, eq
  D_Flip_Flop IDLE_3 (.clk(CLK), .D(Write_ASCII), .Q(IDLE_3_q), .reset(RST));  // open: Qn, preset, en
  Demultiplexer #(.enable("false")) demultiplexer_2 (
    .out0(demultiplexer_2_out0), .out1(demultiplexer_2_out1), .in(IDLE_3_q), .sel(_0_c));
  Bit_Extender #(.in_width(32), .out_width(24)) bit_extender_1 (.in(multiplexer_3_out), .out(bit_extender_1_out));
  D_Flip_Flop IDLE_4 (.clk(CLK), .D(Lc_0), .Q(IDLE_4_q), .reset(RST));  // open: Qn, preset, en
  or or_4 (Lc, Lc_0, Write_ASCII);
  or or_5 (Ln, Ln_0, Lc_0);
  Demultiplexer #(.enable("false")) demultiplexer_3 (
    .out0(demultiplexer_3_out0), .out1(demultiplexer_3_out1), .in(IDLE_4_q), .sel(_0_n));
  D_Flip_Flop IDLE_5 (.clk(CLK), .D(demultiplexer_2_out0), .Q(\end ), .reset(RST));  // open: Qn, preset, en
  MEMORY memory_1 (
    .DIR(bit_extender_1_out), .DATA_IN(n___10___48), .WRITE(Lc_0), .CLK(CLK), .CLR(RST),
    .DATA_OUT(memory_1_data_out));
  Bit_Extender #(.in_width(32), .out_width(7)) bit_extender_2 (.in(memory_1_data_out), .out(ASCII));

  // Other names for the same wires on the sheet: Lc_1 = Write_ASCII; Sc = Write_ASCII; Ln_1 = Lc_0; Sn = Lc_0;
  //   Write = Lc_0
endmodule

module PRINT_DEC (
  input  [31:0] num,
  input  start,
  input  CLK,
  input  RST,
  output [6:0] ASCII,
  output Write_ASCII,
  output END
);

  wire demultiplexer_1_out0, demultiplexer_1_out1, demultiplexer_2_out0, demultiplexer_3_out0, end_t,
       IDLE_3_q, IDLE_q, or_1_out, or_2_out, or_3_out, S_ASCII, startUDEC, Write_ASCII_1;
  wire [6:0] ASCII_t;
  wire [31:0] multiplexer_1_out, negator_1_out;

  or or_1 (or_1_out, demultiplexer_1_out0, END);
  Negator #(.width(32)) negator_1 (.in(num), .out(negator_1_out));
  D_Flip_Flop IDLE (.clk(CLK), .D(or_1_out), .Q(IDLE_q), .preset(RST));  // open: Qn, en, reset
  Demultiplexer #(.enable("false")) demultiplexer_1 (
    .out0(demultiplexer_1_out0), .out1(demultiplexer_1_out1), .in(IDLE_q), .sel(start));
  Multiplexer #(.width(32), .enable("false")) multiplexer_1 (
    .in0(num), .in1(negator_1_out), .out(multiplexer_1_out), .sel(num[31]));
  Demultiplexer #(.enable("false")) demultiplexer_2 (
    .out0(demultiplexer_2_out0), .out1(S_ASCII), .in(demultiplexer_1_out1), .sel(num[31]));
  or or_2 (or_2_out, demultiplexer_2_out0, S_ASCII);
  D_Flip_Flop IDLE_2 (.clk(CLK), .D(or_2_out), .Q(startUDEC), .reset(RST));  // open: Qn, preset, en
  PRINT_UDEC print_udec_1 (
    .num(multiplexer_1_out), .start(startUDEC), .CLK(CLK), .RST(RST), .ASCII(ASCII_t),
    .Write_ASCII(Write_ASCII_1), .\end (end_t));
  D_Flip_Flop IDLE_3 (.clk(CLK), .D(or_3_out), .Q(IDLE_3_q), .reset(RST));  // open: Qn, preset, en
  or or_3 (or_3_out, startUDEC, demultiplexer_3_out0);
  Demultiplexer #(.enable("false")) demultiplexer_3 (
    .out0(demultiplexer_3_out0), .out1(END), .in(IDLE_3_q), .sel(end_t));
  Multiplexer #(.width(7), .enable("false")) multiplexer_2 (
    .in0(ASCII_t), .in1(7'b0101101), .out(ASCII), .sel(S_ASCII));
  or or_4 (Write_ASCII, S_ASCII, Write_ASCII_1);

  // Other names for the same wires on the sheet: sign = num[31]; Write_ASCII_0 = S_ASCII
endmodule

module TEST_PRINT (
  input  [31:0] in_1,
  output out_2
);

  wire button_1_out, button_2_out, CLK, CLR, d_ff_1_q, Write_ASCII;
  wire [6:0] ASCII;

  Button button_1 (.out(button_1_out));
  Clock clock_1 (.out(CLK));
  D_Flip_Flop d_ff_1 (.clk(CLK), .D(1'b1), .Q(d_ff_1_q), .reset(button_1_out));  // open: Qn, preset, en
  D_Flip_Flop d_ff_2 (.clk(CLK), .D(d_ff_1_q), .Qn(CLR), .reset(button_1_out));  // open: Q, preset, en
  Button button_2 (.out(button_2_out));
  PRINT_UDEC print_udec_1 ();  // open: num, start, CLK, RST, ASCII, Write_ASCII, end
  PRINT_DEC print_dec_1 (
    .num(in_1), .start(button_2_out), .CLK(CLK), .RST(CLR), .ASCII(ASCII), .Write_ASCII(Write_ASCII),
    .END(out_2));
  TTY #(.rows(32), .cols(60)) tty_1 (.data(ASCII), .clk(CLK), .we(Write_ASCII), .clr(CLR));
endmodule

module data_path (
  input  clk,
  input  enable_eax,
  input  enable_ll,
  input  [31:0] ram_in,
  input  [31:0] input_in,
  input  i_in,
  input  j_in,
  input  k_in,
  input  i1,
  input  ram_selector,
  input  i2,
  input  i3,
  input  i4,
  input  clr,
  output [31:0] ram_out,
  output [23:0] ram_addr,
  output [23:0] input_addr,
  output i___L_len,
  output j___R_len,
  output L_i_____R_j
);

  wire [23:0] adder_8_out, i_addr, j_addr, k_addr, l_i, multiplexer_3_out, multiplexer_4_out,
       multiplexer_5_out, multiplexer_6_out, multiplexer_8_out, r, r_j, r_len, xor_1_out;
  wire [31:0] eax, i, i_1, j, j_1, k, k_1, L_len, ram_in_t;
  wire [31:24] i_out, j_out, k_out;

  Adder #(.width(32)) adder_1 (.a({i_out, i_addr}), .b(32'h1), .out(i_1));  // open: cin, cout
  Adder #(.width(32)) adder_2 (.a({j_out, j_addr}), .b(32'h1), .out(j_1));  // open: cin, cout
  Adder #(.width(32)) adder_3 (.a({k_out, k_addr}), .b(32'h1), .out(k_1));  // open: cin, cout
  Register #(.width(32), .trigger("falling")) u_i (.D(i), .en(i_in), .Q({i_out, i_addr}), .clk(clk));  // open: clr
  Multiplexer #(.width(32), .disabled(0), .enable("false")) multiplexer_1 (
    .in0(ram_in), .in1({32{1'b0}}), .out(ram_in_t), .sel(clr));
  Multiplexer #(.width(32), .disabled(0), .enable("false")) multiplexer_2 (
    .in0(input_in), .in1({32{1'b0}}), .out(ram_out), .sel(clr));
  Multiplexer #(.width(24), .enable("false")) multiplexer_3 (
    .in0({24{1'b0}}), .in1({24{1'b0}}), .out(multiplexer_3_out), .sel(i1));
  Multiplexer #(.width(24), .enable("false")) multiplexer_4 (
    .in0({24{1'b0}}), .in1(l_i), .out(multiplexer_4_out), .sel(i2));
  Multiplexer #(.width(24), .enable("false")) multiplexer_5 (
    .in0({24{1'b0}}), .in1(r_len), .out(multiplexer_5_out), .sel(i3));
  Multiplexer #(.width(24), .enable("false")) multiplexer_6 (
    .in0({24{1'b0}}), .in1(r_j), .out(multiplexer_6_out), .sel(i4));
  Register #(.width(32), .trigger("high")) u_eax (.D(ram_out), .en(enable_eax), .Q(eax), .clk(clk));  // open: clr
  Register #(.width(32), .trigger("high")) u_l_len (.D(ram_out), .en(enable_ll), .Q(L_len), .clk(clk));  // open: clr
  Adder #(.width(24)) adder_4 (.a(24'h1), .b(L_len[23:0]), .out(r_len));  // open: cin, cout
  Adder #(.width(24)) adder_5 (.a(r_len), .b(24'h1), .out(r));  // open: cin, cout
  Register #(.width(32), .trigger("falling")) u_j (.D(j), .en(j_in), .Q({j_out, j_addr}), .clk(clk));  // open: clr
  Adder #(.width(24)) adder_6 (.a(24'h1), .b(i_addr), .out(l_i));  // open: cin, cout
  Adder #(.width(24)) adder_7 (.a(r), .b(j_addr), .out(r_j));  // open: cin, cout
  ExactlyOne xor_1[23:0] (
    .out(xor_1_out), .in0(multiplexer_3_out), .in1(multiplexer_4_out), .in2(multiplexer_5_out),
    .in3(multiplexer_6_out));
  Multiplexer #(.width(24), .disabled(0), .enable("false")) multiplexer_7 (
    .in0(xor_1_out), .in1({24{1'b0}}), .out(input_addr), .sel(clr));
  Register #(.width(32), .trigger("falling")) u_k (.D(k), .en(k_in), .Q({k_out, k_addr}), .clk(clk));  // open: clr
  // Probe on adder_8_out
  Comparator #(.width(32), .mode("unsigned")) comparator_1 (
    .a({i_out, i_addr}), .b(L_len), .lt(i___L_len));  // open: gt, eq
  Comparator #(.width(32), .mode("unsigned")) comparator_2 (
    .a({j_out, j_addr}), .b(ram_out), .lt(j___R_len));  // open: gt, eq
  Comparator #(.width(32), .mode("unsigned")) comparator_3 (.a(eax), .b(ram_out), .gt(L_i_____R_j));  // open: eq, lt
  Adder #(.width(24)) adder_8 (.a(24'hffff98), .b(k_addr), .out(adder_8_out));  // open: cin, cout
  Multiplexer #(.width(24), .enable("false")) multiplexer_8 (
    .in0({24{1'b0}}), .in1(adder_8_out), .out(multiplexer_8_out), .sel(ram_selector));
  Multiplexer #(.width(32), .enable("false")) multiplexer_9 (.in0({32{1'b0}}), .in1(i_1), .out(i), .sel(i_in));
  Multiplexer #(.width(24), .disabled(0), .enable("false")) multiplexer_10 (
    .in0(multiplexer_8_out), .in1({24{1'b0}}), .out(ram_addr), .sel(clr));
  Multiplexer #(.width(32), .enable("false")) multiplexer_11 (.in0({32{1'b0}}), .in1(j_1), .out(j), .sel(j_in));
  Multiplexer #(.width(32), .enable("false")) multiplexer_12 (.in0({32{1'b0}}), .in1(k_1), .out(k), .sel(k_in));

  // Other names for the same wires on the sheet: i_out[23:0] = i_addr; input_in_t[31:0] = ram_out;
  //   j_out[23:0] = j_addr; k_out[23:0] = k_addr; ll_addr[23:0] = L_len[23:0]; Si = i_in; Sj = j_in; Sk = k_in
endmodule

module cpu (
  input  clk,
  input  [31:0] data,
  input  clr,
  input  [31:0] ram_data,
  output \end ,
  output [23:0] input_addr,
  output [23:0] ram_addr,
  output [31:0] write_in_ram,
  output ram_write
);

  wire cont, cont_3, continue_loop, demultiplexer_1_out0, demultiplexer_2_out1, demultiplexer_3_out1,
       demultiplexer_4_out1, e_alen, eax, \else , end_t, i2, i2_a, i2_c, i3, i3_a, i3_b, i4, i4_b, i4_c,
       i___L_len, i_in, i_in_a, i_in_b, idle, idle_q, j___R_len, j_in, j_in_a, j_in_b, k_in, k_in_a,
       L_i_____R_j, loop, loop_2, loop_3, loop_end, main_cond, main_end, or_1_out, or_12_out, or_13_out, ram,
       start;

  Button button_1 (.out(start));
  or or_1 (or_1_out, 1'b1, idle);
  D_Flip_Flop \wait  (.clk(clk), .D(demultiplexer_2_out1), .Q(cont));  // open: Qn, preset, en, reset
  D_Flip_Flop u_idle (.clk(clk), .D(or_1_out), .Q(idle_q));  // open: Qn, preset, en, reset
  Demultiplexer #(.enable("false")) demultiplexer_1 (
    .out0(demultiplexer_1_out0), .out1(e_alen), .in(idle_q), .sel(start));
  D_Flip_Flop d_ff_1 (.clk(clk), .D(cont), .Q(i_in_a));  // open: Qn, preset, en, reset
  data_path data_path_1 (
    .clk(clk), .enable_eax(eax), .ram_in(ram_data), .input_in(data), .i_in(i_in), .j_in(j_in), .k_in(k_in),
    .clr(clr), .ram_out(write_in_ram), .ram_addr(ram_addr), .input_addr(input_addr), .i___L_len(i___L_len),
    .j___R_len(j___R_len), .L_i_____R_j(L_i_____R_j), .i1(e_alen), .i3(i3), .i4(i4), .ram_selector(ram),
    .enable_ll(e_alen), .i2(i2));
  Demultiplexer #(.enable("false")) demultiplexer_2 (
    .out0(\else ), .out1(demultiplexer_2_out1), .in(i2_a), .sel(L_i_____R_j));
  or or_2 (i3_a, continue_loop, loop);
  D_Flip_Flop while_1 (.clk(clk), .D(e_alen), .Q(loop));  // open: Qn, preset, en, reset
  D_Flip_Flop wait_write_i (.clk(clk), .D(eax), .Q(i2_a));  // open: Qn, preset, en, reset
  D_Flip_Flop d_ff_2 (.clk(clk), .D(i_in_a), .Q(main_end));  // open: Qn, preset, en, reset
  or or_3 (i2, i2_a, i2_c, cont);
  or or_4 (i4, eax, i4_c, i4_b);
  or or_5 (i3, i3_a, i3_b);
  and and_1 (main_cond, i___L_len, j___R_len);
  or or_6 (k_in, k_in_a, i_in_b, j_in_b);
  Demultiplexer #(.disabled(0), .enable("false")) demultiplexer_3 (
    .out0(loop_2), .out1(demultiplexer_3_out1), .in(i3_a), .sel(main_cond));
  or or_7 (ram_write, cont, i4_b, i2_c, i4_c);
  D_Flip_Flop while_1_2 (.clk(clk), .D(demultiplexer_3_out1), .Q(eax));  // open: Qn, preset, en, reset
  D_Flip_Flop d_ff_3 (.clk(clk), .D(\else ), .Q(i4_b));  // open: Qn, preset, en, reset
  or or_8 (ram, i4_b, cont, i2_c, i4_c);
  or or_9 (i_in, i_in_a, i_in_b);
  or or_10 (j_in, j_in_a, j_in_b);
  or or_11 (i3_b, cont_3, loop_3);
  Demultiplexer #(.disabled(0), .enable("false")) demultiplexer_4 (
    .out0(loop_end), .out1(demultiplexer_4_out1), .in(i3_b), .sel(j___R_len));
  D_Flip_Flop u_end (.clk(clk), .D(or_12_out), .Q(\end ));  // open: Qn, preset, en, reset
  or or_12 (or_12_out, loop_end, end_t);
  D_Flip_Flop wait_write (.clk(clk), .D(i4_b), .Q(j_in_a));  // open: Qn, preset, en, reset
  Demultiplexer #(.disabled(0), .enable("false")) demultiplexer_5 (
    .out0(loop_3), .out1(i2_c), .in(or_13_out), .sel(i___L_len));
  or or_13 (or_13_out, i_in_b, loop_2);
  D_Flip_Flop wait_2 (.clk(clk), .D(j_in_b), .Q(cont_3));  // open: Qn, preset, en, reset
  D_Flip_Flop d_ff_4 (.clk(clk), .D(demultiplexer_4_out1), .Q(i4_c));  // open: Qn, preset, en, reset
  Demultiplexer #(.enable("false")) demultiplexer_6 (.out0(end_t), .out1(idle), .in(\end ), .sel(start));
  D_Flip_Flop d_ff_5 (.clk(clk), .D(i2_c), .Q(i_in_b));  // open: Qn, preset, en, reset
  D_Flip_Flop d_ff_6 (.clk(clk), .D(i4_c), .Q(j_in_b));  // open: Qn, preset, en, reset
  or or_14 (k_in_a, j_in_a, main_end);
  D_Flip_Flop d_ff_7 (.clk(clk), .D(k_in_a), .Q(continue_loop));  // open: Qn, preset, en, reset

  // Other names for the same wires on the sheet: D_IN[23:0] = input_addr; D_OUT[31:0] = data; finish = \end ;
  //   i1 = e_alen; i4_a = eax; k_in_b = i_in_b; k_in_c = j_in_b; ram_in[31:0] = write_in_ram;
  //   ram_out[31:0] = ram_data; i2_b = cont; ram_b = cont; ram_write_a = cont; ram_a = i4_b; ram_write_b = i4_b;
  //   ram_c = i2_c; ram_write_c = i2_c; ram_d = i4_c; ram_write_d = i4_c
endmodule
