// Logisim project BigASM.circ as structural Verilog
module BOARD_BIG_ASM (
  output out_1
);

  wire button_1_out, CLK, CLR, d_ff_1_q, not_1_out, Write, Write_ASCII;
  wire [6:0] ASCII;
  wire [7:0] counter_1_q;
  wire [23:0] Dir_INPUT, Dir_MEMORY;
  wire [31:0] INPUT, MEMORY_IN, MEMORY_OUT;

  Button button_1 (.out(button_1_out));
  Clock clock_1 (.out(CLK));
  D_Flip_Flop d_ff_1 (.clk(CLK), .D(1'b1), .Q(d_ff_1_q), .reset(button_1_out));  // open: Qn, preset, en
  D_Flip_Flop d_ff_2 (.clk(CLK), .D(d_ff_1_q), .Qn(CLR), .reset(button_1_out));  // open: Q, preset, en
  BIG_ASM big_asm_1 (
    .DATA_INPUT(INPUT), .MEMORY_IN(MEMORY_OUT), .CLK(CLK), .CLR(CLR), .DIR_INPUT(Dir_INPUT),
    .MEMORY_OUT(MEMORY_IN), .DIR_MEMORY(Dir_MEMORY), .Write_OUTPUT(Write), .ASCII(ASCII),
    .Write_ASCII(Write_ASCII), .END(out_1));
  MEMORY memory_1 (.DIR(Dir_MEMORY), .DATA_IN(MEMORY_IN), .WRITE(Write), .CLK(CLK), .CLR(CLR), .DATA_OUT(MEMORY_OUT));
  INPUT input_1 (.DIR(Dir_INPUT), .CLK(CLK), .DATA_OUT(INPUT));
  Counter counter_1 (.load(1'b0), .count(not_1_out), .Q(counter_1_q), .clk(CLK), .clr(CLR));  // open: D, carry
  not not_1 (not_1_out, out_1);
  // Probe on counter_1_q
  TTY #(.rows(32), .cols(60)) tty_1 (.data(ASCII), .clk(CLK), .we(Write_ASCII), .clr(CLR));

  // Other names for the same wires on the sheet: END = out_1

  // Notes on the sheet:
  //   COUNTER
  //   BOARD
endmodule

module INPUT (
  input  [23:0] DIR,
  input  CLK,
  output [31:0] DATA_OUT
);

  RAM #(.addrWidth(24), .dataWidth(32)) ram_1 (.addr(DIR), .data(DATA_OUT), .clk(CLK), .ld(1'b1));  // open: sel, clr
endmodule

module MEMORY (
  input  [23:0] DIR,
  input  [31:0] DATA_IN,
  input  WRITE,
  input  CLK,
  input  CLR,
  output [31:0] DATA_OUT
);

  wire not_1_out;

  not not_1 (not_1_out, WRITE);
  RAM #(.addrWidth(24), .dataWidth(32), .bus("separate")) ram_1 (
    .addr(DIR), .din(DATA_IN), .data(DATA_OUT), .clk(CLK), .ld(not_1_out), .clr(CLR));  // open: str, sel
endmodule

module BIG_ASM (
  input  [31:0] DATA_INPUT,
  input  [31:0] MEMORY_IN,
  input  CLK,
  input  CLR,
  output [23:0] DIR_INPUT,
  output [31:0] MEMORY_OUT,
  output [23:0] DIR_MEMORY,
  output Write_OUTPUT,
  output [6:0] ASCII,
  output Write_ASCII,
  output END
);

  wire and_1_out, and_2_out, button_1_out, contol_unit_1_ld, contol_unit_1_lm, contol_unit_1_ly,
       contol_unit_1_out_5, contol_unit_1_out_6, CU, demultiplexer_1_out1, demultiplexer_1_out2,
       demultiplexer_1_out3, L0, L1, L2, L3, L4, L5, not_1_out, not_2_out, PRINT, print_udec_1_end, PW, s0,
       s1, sPrinter, W_ASCII, Y_24;
  wire [1:0] counter_1_q;
  wire [6:0] ASCII_t;
  wire [31:0] out;

  and and_1 (and_1_out, PRINT, not_1_out);
  not not_1 (not_1_out, END);
  PRINT_UDEC print_udec_1 (
    .num(out), .start(and_1_out), .CLK(CLK), .RST(CLR), .ASCII(ASCII_t), .Write_ASCII(W_ASCII),
    .\end (print_udec_1_end));
  Demultiplexer #(.select(2)) demultiplexer_1 (
    .out1(demultiplexer_1_out1), .out2(demultiplexer_1_out2), .out3(demultiplexer_1_out3), .in(1'b1),
    .sel(counter_1_q));  // open: out0, en
  and and_2 (and_2_out, print_udec_1_end, not_2_out);
  not not_2 (not_2_out, END);
  Button button_1 (.out(button_1_out));
  Counter #(.width(2), .max('h3)) counter_1 (
    .count(and_2_out), .Q(counter_1_q), .carry(END), .clk(CLK), .clr(CLR));  // open: load, D
  Contol_Unit contol_unit_1 (
    .START(CU), .Y_24(Y_24), .out_5(contol_unit_1_out_5), .out_6(contol_unit_1_out_6), .LD(contol_unit_1_ld),
    .LM(contol_unit_1_lm), .LY(contol_unit_1_ly), .CLK(CLK), .END(sPrinter), .CLR(CLR));
  Printer printer_1 (
    .start(sPrinter), .CLK(CLK), .PRINTDAY(demultiplexer_1_out1), .PRINTMONTH(demultiplexer_1_out2),
    .PRINTYEAR(demultiplexer_1_out3), .SOUT_0(s0), .SOUT_1(s1), .CLR(CLR), .PRINT(PRINT), .PW(PW));
  Loader loader_1 (
    .CLK(CLK), .CLR(CLR), .START(button_1_out), .L0(L0), .L1(L1), .L2(L2), .L3(L3), .L4(L4), .L5(L5), .END(CU));
  Data_Path data_path_1 (
    .Sy0(contol_unit_1_out_5), .Sy1(contol_unit_1_out_6), .LD(contol_unit_1_ld), .LM(contol_unit_1_lm),
    .LY(contol_unit_1_ly), .CLK(CLK), .CLR(CLR), .Data_out(out), .Y_24(Y_24), .SOUT0(s0), .SOUT1(s1),
    .DATA_IN(DATA_INPUT), .L0(L0), .L1(L1), .L2(L2), .L3(L3), .L4(L4), .L5(L5), .dIR(DIR_INPUT));
  Multiplexer #(.width(7)) multiplexer_1 (.in0(ASCII_t), .in1(7'b0100000), .out(ASCII), .sel(PW));  // open: en
  or or_1 (Write_ASCII, W_ASCII, PW);

  // Other names for the same wires on the sheet: DI[31:0] = DATA_INPUT; dIR[23:0] = DIR_INPUT
endmodule

module PRINT_UDEC (
  input  [31:0] num,
  input  start,
  input  CLK,
  input  RST,
  output [6:0] ASCII,
  output Write_ASCII,
  output \end 
);

  wire _0_c, _0_n, demultiplexer_1_out0, demultiplexer_2_out0, demultiplexer_2_out1, demultiplexer_3_out0,
       demultiplexer_3_out1, IDLE_2_q, IDLE_3_q, IDLE_4_q, IDLE_q, Lc, Lc_0, Ln, Ln_0, or_1_out;
  wire [23:0] bit_extender_1_out;
  wire [31:0] c, c___1, c___1_t, divider_1_rem, memory_1_data_out, multiplexer_1_out, multiplexer_2_out,
       multiplexer_3_out, n, n___10, n___10___48;

  Multiplexer #(.width(32), .enable("false")) multiplexer_1 (
    .in0(num), .in1(n___10), .out(multiplexer_1_out), .sel(Lc_0));
  Divider #(.width(32)) divider_1 (.a(n), .b(32'ha), .out(n___10), .rem(divider_1_rem));  // open: upper
  Adder #(.width(32)) adder_1 (.a(divider_1_rem), .b(32'h30), .out(n___10___48));  // open: cin, cout
  or or_1 (or_1_out, demultiplexer_1_out0, \end );
  Register #(.width(32)) u_n (.D(multiplexer_1_out), .en(Ln), .Q(n), .clk(CLK), .clr(RST));
  D_Flip_Flop IDLE (.clk(CLK), .D(or_1_out), .Q(IDLE_q), .preset(RST));  // open: Qn, en, reset
  Demultiplexer #(.enable("false")) demultiplexer_1 (
    .out0(demultiplexer_1_out0), .out1(Ln_0), .in(IDLE_q), .sel(start));
  or or_2 (Write_ASCII, demultiplexer_3_out0, demultiplexer_2_out1);
  Multiplexer #(.width(32), .enable("false")) multiplexer_2 (
    .in0(c___1), .in1(c___1_t), .out(multiplexer_2_out), .sel(Write_ASCII));
  Adder #(.width(32)) adder_2 (.a(c), .b(32'h1), .out(c___1));  // open: cin, cout
  Subtractor #(.width(32)) subtractor_1 (.a(c), .b(32'h1), .out(c___1_t));  // open: bin, bout
  D_Flip_Flop IDLE_2 (.clk(CLK), .D(Ln_0), .Q(IDLE_2_q), .reset(RST));  // open: Qn, preset, en
  Register #(.width(32)) u_c (.D(multiplexer_2_out), .en(Lc), .Q(c), .clk(CLK), .clr(RST));
  or or_3 (Lc_0, IDLE_2_q, demultiplexer_3_out1);
  Multiplexer #(.width(32), .enable("false")) multiplexer_3 (
    .in0(c), .in1(c___1_t), .out(multiplexer_3_out), .sel(Write_ASCII));
  Comparator #(.width(32), .mode("unsigned")) comparator_1 (.a({32{1'b0}}), .b(n), .lt(_0_n));  // open: gt, eq
  Comparator #(.width(32), .mode("unsigned")) comparator_2 (.a({32{1'b0}}), .b(c), .lt(_0_c));  // open: gt, eq
  D_Flip_Flop IDLE_3 (.clk(CLK), .D(Write_ASCII), .Q(IDLE_3_q), .reset(RST));  // open: Qn, preset, en
  Demultiplexer #(.enable("false")) demultiplexer_2 (
    .out0(demultiplexer_2_out0), .out1(demultiplexer_2_out1), .in(IDLE_3_q), .sel(_0_c));
  Bit_Extender #(.in_width(32), .out_width(24)) bit_extender_1 (.in(multiplexer_3_out), .out(bit_extender_1_out));
  D_Flip_Flop IDLE_4 (.clk(CLK), .D(Lc_0), .Q(IDLE_4_q), .reset(RST));  // open: Qn, preset, en
  or or_4 (Lc, Lc_0, Write_ASCII);
  or or_5 (Ln, Ln_0, Lc_0);
  Demultiplexer #(.enable("false")) demultiplexer_3 (
    .out0(demultiplexer_3_out0), .out1(demultiplexer_3_out1), .in(IDLE_4_q), .sel(_0_n));
  D_Flip_Flop IDLE_5 (.clk(CLK), .D(demultiplexer_2_out0), .Q(\end ), .reset(RST));  // open: Qn, preset, en
  MEMORY memory_1 (
    .DIR(bit_extender_1_out), .DATA_IN(n___10___48), .WRITE(Lc_0), .CLK(CLK), .CLR(RST),
    .DATA_OUT(memory_1_data_out));
  Bit_Extender #(.in_width(32), .out_width(7)) bit_extender_2 (.in(memory_1_data_out), .out(ASCII));

  // Other names for the same wires on the sheet: Lc_1 = Write_ASCII; Sc = Write_ASCII; Ln_1 = Lc_0; Sn = Lc_0;
  //   Write = Lc_0
endmodule

module PRINT_DEC (
  input  [31:0] num,
  input  start,
  input  CLK,
  input  RST,
  output [6:0] ASCII,
  output Write_ASCII,
  output END
);

  wire demultiplexer_1_out0, demultiplexer_1_out1, demultiplexer_2_out0, demultiplexer_3_out0, end_t,
       IDLE_3_q, IDLE_q, or_1_out, or_2_out, or_3_out, S_ASCII, startUDEC, Write_ASCII_1;
  wire [6:0] ASCII_t;
  wire [31:0] multiplexer_1_out, negator_1_out;

  or or_1 (or_1_out, demultiplexer_1_out0, END);
  Negator #(.width(32)) negator_1 (.in(num), .out(negator_1_out));
  D_Flip_Flop IDLE (.clk(CLK), .D(or_1_out), .Q(IDLE_q), .preset(RST));  // open: Qn, en, reset
  Demultiplexer #(.enable("false")) demultiplexer_1 (
    .out0(demultiplexer_1_out0), .out1(demultiplexer_1_out1), .in(IDLE_q), .sel(start));
  Multiplexer #(.width(32), .enable("false")) multiplexer_1 (
    .in0(num), .in1(negator_1_out), .out(multiplexer_1_out), .sel(num[31]));
  Demultiplexer #(.enable("false")) demultiplexer_2 (
    .out0(demultiplexer_2_out0), .out1(S_ASCII), .in(demultiplexer_1_out1), .sel(num[31]));
  or or_2 (or_2_out, demultiplexer_2_out0, S_ASCII);
  D_Flip_Flop IDLE_2 (.clk(CLK), .D(or_2_out), .Q(startUDEC), .reset(RST));  // open: Qn, preset, en
  PRINT_UDEC print_udec_1 (
    .num(multiplexer_1_out), .start(startUDEC), .CLK(CLK), .RST(RST), .ASCII(ASCII_t),
    .Write_ASCII(Write_ASCII_1), .\end (end_t));
  D_Flip_Flop IDLE_3 (.clk(CLK), .D(or_3_out), .Q(IDLE_3_q), .reset(RST));  // open: Qn, preset, en
  or or_3 (or_3_out, startUDEC, demultiplexer_3_out0);
  Demultiplexer #(.enable("false")) demultiplexer_3 (
    .out0(demultiplexer_3_out0), .out1(END), .in(IDLE_3_q), .sel(end_t));
  Multiplexer #(.width(7), .enable("false")) multiplexer_2 (
    .in0(ASCII_t), .in1(7'b0101101), .out(ASCII), .sel(S_ASCII));
  or or_4 (Write_ASCII, S_ASCII, Write_ASCII_1);

  // Other names for the same wires on the sheet: sign = num[31]; Write_ASCII_0 = S_ASCII
endmodule

module TEST_PRINT (
  input  [31:0] in_1,
  output out_2
);

  wire button_1_out, button_2_out, CLK, CLR, d_ff_1_q, Write_ASCII;
  wire [6:0] ASCII;

  Button button_1 (.out(button_1_out));
  Clock clock_1 (.out(CLK));
  D_Flip_Flop d_ff_1 (.clk(CLK), .D(1'b1), .Q(d_ff_1_q), .reset(button_1_out));  // open: Qn, preset, en
  D_Flip_Flop d_ff_2 (.clk(CLK), .D(d_ff_1_q), .Qn(CLR), .reset(button_1_out));  // open: Q, preset, en
  Button button_2 (.out(button_2_out));
  PRINT_UDEC print_udec_1 ();  // open: num, start, CLK, RST, ASCII, Write_ASCII, end
  PRINT_DEC print_dec_1 (
    .num(in_1), .start(button_2_out), .CLK(CLK), .RST(CLR), .ASCII(ASCII), .Write_ASCII(Write_ASCII),
    .END(out_2));
  TTY #(.rows(32), .cols(60)) tty_1 (.data(ASCII), .clk(CLK), .we(Write_ASCII), .clr(CLR));
endmodule

module Data_Path (
  input  Sy0,
  input  Sy1,
  input  [31:0] DATA_IN,
  input  L0,
  input  L1,
  input  L2,
  input  L3,
  input  L4,
  input  L5,
  input  LD,
  input  LM,
  input  LY,
  input  CLK,
  input  SOUT0,
  input  SOUT1,
  input  CLR,
  output [31:0] Data_out,
  output [23:0] dIR,
  output Y_24
);

  wire and_1_out, comparator_1_eq, or_1_out, STOP;
  wire [31:0] D, M, multiplexer_2_out, multiplier_1_out, multiplier_2_out, multiplier_3_out, w0, w0_10_w1,
       w1, w2, w2_10_w3, w3, w4, w4_10_w5, w5, Y, Y___1900, Y___2000;

  or or_1 (or_1_out, L0, L1, L2, L3, L4, L5);
  and and_1 (and_1_out, or_1_out, STOP);
  Register #(.width(32)) u_D (.D(w4_10_w5), .en(LD), .Q(D), .clk(CLK), .clr(CLR));
  // Probe on D
  Counter #(.width(24), .max('hffffff)) PC (
    .D({24{1'b0}}), .count(and_1_out), .Q(dIR), .clk(CLK), .clr(CLR));  // open: load, carry
  Multiplexer #(.select(2), .width(32)) multiplexer_1 (
    .in0(D), .in1(M), .in2(Y), .out(Data_out), .sel({SOUT1, SOUT0}));  // open: in3, en
  Register #(.width(32)) u_M (.D(w2_10_w3), .en(LM), .Q(M), .clk(CLK), .clr(CLR));
  // Probe on M
  Multiplexer #(.select(2), .width(32)) multiplexer_2 (
    .in1(Y___2000), .in2(Y___1900), .out(multiplexer_2_out), .sel({Sy1, Sy0}), .en(LY));  // open: in0, in3
  // Probe on 32'ha
  // Probe on 32'ha
  // Probe on 32'ha
  Register #(.width(32)) u_Y (.D(multiplexer_2_out), .en(LY), .Q(Y), .clk(CLK), .clr(CLR));
  Multiplier #(.width(32)) multiplier_1 (.a(w0), .b(32'ha), .out(multiplier_1_out));  // open: cin, cout
  Multiplier #(.width(32)) multiplier_2 (.a(w2), .b(32'ha), .out(multiplier_2_out));  // open: cin, cout
  Multiplier #(.width(32)) multiplier_3 (.a(w4), .b(32'ha), .out(multiplier_3_out));  // open: cin, cout
  // Probe on Y
  Adder #(.width(32)) adder_1 (.a(w1), .b(multiplier_1_out), .out(w0_10_w1));  // open: cin, cout
  Adder #(.width(32)) adder_2 (.a(w3), .b(multiplier_2_out), .out(w2_10_w3));  // open: cin, cout
  Adder #(.width(32)) adder_3 (.a(w5), .b(multiplier_3_out), .out(w4_10_w5));  // open: cin, cout
  Register #(.width(32)) D0 (.D(DATA_IN), .en(L0), .Q(w0), .clk(CLK), .clr(CLR));
  Register #(.width(32)) D1 (.D(DATA_IN), .en(L1), .Q(w1), .clk(CLK), .clr(CLR));
  Register #(.width(32)) D2 (.D(DATA_IN), .en(L2), .Q(w2), .clk(CLK), .clr(CLR));
  Register #(.width(32)) D3 (.D(DATA_IN), .en(L3), .Q(w3), .clk(CLK), .clr(CLR));
  Register #(.width(32)) D4 (.D(DATA_IN), .en(L4), .Q(w4), .clk(CLK), .clr(CLR));
  Register #(.width(32)) D5 (.D(DATA_IN), .en(L5), .Q(w5), .clk(CLK), .clr(CLR));
  // Probe on 32'h76c
  // Probe on 32'h7d0
  // Probe on 32'h18
  Comparator #(.width(24), .mode("unsigned")) comparator_1 (.a(dIR), .b(24'h6), .eq(comparator_1_eq));  // open: gt, lt
  Adder #(.width(32)) adder_4 (.a(w0_10_w1), .b(32'h76c), .out(Y___1900));  // open: cin, cout
  Adder #(.width(32)) adder_5 (.a(w0_10_w1), .b(32'h7d0), .out(Y___2000));  // open: cin, cout
  Comparator #(.width(32), .mode("unsigned")) comparator_2 (.a(w0_10_w1), .b(32'h18), .gt(Y_24));  // open: eq, lt
  not not_1 (STOP, comparator_1_eq);

  // Other names for the same wires on the sheet: DI[31:0] = DATA_IN; Dout[31:0] = Data_out

  // Notes on the sheet:
  //   DATA PATH
endmodule

module Contol_Unit (
  input  START,
  input  CLK,
  input  Y_24,
  input  CLR,
  output out_5,
  output out_6,
  output LD,
  output LM,
  output LY,
  output END
);

  wire demultiplexer_1_out0, demultiplexer_3_out0, demultiplexer_3_out1, IDLE_q, not_1_out, or_1_out,
       or_2_out, STARTER;

  or or_1 (or_1_out, demultiplexer_1_out0, demultiplexer_3_out1);
  D_Flip_Flop IDLE (.clk(CLK), .D(or_1_out), .Q(IDLE_q), .preset(CLR));  // open: Qn, en, reset
  Demultiplexer demultiplexer_1 (.out0(demultiplexer_1_out0), .out1(LD), .in(IDLE_q), .sel(STARTER));  // open: en
  and and_1 (STARTER, START, not_1_out);
  not not_1 (not_1_out, END);
  Demultiplexer demultiplexer_2 (.out0(out_5), .out1(out_6), .in(LD), .sel(Y_24));  // open: en
  or or_2 (or_2_out, demultiplexer_3_out0, out_5, out_6);
  D_Flip_Flop u_END (.clk(CLK), .D(or_2_out), .Q(END), .reset(CLR));  // open: Qn, preset, en
  Demultiplexer demultiplexer_3 (
    .out0(demultiplexer_3_out0), .out1(demultiplexer_3_out1), .in(END), .sel(STARTER));  // open: en

  assign LM = LD;
  assign LY = LD;

  // Other names for the same wires on the sheet: sy0 = out_5; sy1 = out_6

  // Notes on the sheet:
  //   CONTROL UNIT
endmodule

module Printer (
  input  start,
  input  CLK,
  input  PRINTDAY,
  input  PRINTMONTH,
  input  PRINTYEAR,
  input  CLR,
  output PRINT,
  output SOUT_0,
  output SOUT_1,
  output PW
);

  wire and_1_out, and_2_out, demultiplexer_1_out0, demultiplexer_1_out1, demultiplexer_2_out0,
       demultiplexer_3_out0, demultiplexer_4_out0, demultiplexer_4_out1, demultiplexer_5_out0,
       demultiplexer_5_out1, END_q, IDLE_q, not_1_out, not_2_out, nPW1, nPW2, or_1_out, or_2_out, or_3_out,
       or_5_out, or_7_out, PRINT1, PW1, PW2;

  or or_1 (or_1_out, demultiplexer_1_out0, demultiplexer_5_out1);
  Demultiplexer #(.disabled(0)) demultiplexer_1 (
    .out0(demultiplexer_1_out0), .out1(demultiplexer_1_out1), .in(IDLE_q), .sel(start));  // open: en
  D_Flip_Flop IDLE (.clk(CLK), .D(or_1_out), .Q(IDLE_q), .preset(1'b1));  // open: Qn, en, reset
  D_Flip_Flop DAY (.clk(CLK), .D(demultiplexer_1_out1), .Q(PRINT1), .reset(CLR));  // open: Qn, preset, en
  or or_2 (or_2_out, demultiplexer_2_out0, PRINT1);
  Demultiplexer #(.disabled(0)) demultiplexer_2 (
    .out0(demultiplexer_2_out0), .out1(SOUT_0), .in(or_2_out), .sel(PRINTDAY));  // open: en
  D_Flip_Flop u_pw (.clk(CLK), .D(SOUT_0), .Q(PW1), .reset(CLR));  // open: Qn, preset, en
  D_Flip_Flop MONTH (.clk(CLK), .D(PW1), .Q(nPW1), .reset(CLR));  // open: Qn, preset, en
  Demultiplexer #(.disabled(0)) demultiplexer_3 (
    .out0(demultiplexer_3_out0), .out1(SOUT_1), .in(or_3_out), .sel(PRINTMONTH));  // open: en
  or or_3 (or_3_out, demultiplexer_3_out0, nPW1);
  or or_4 (PRINT, PRINT1, nPW1, nPW2);
  D_Flip_Flop YEAR (.clk(CLK), .D(PW2), .Q(nPW2), .reset(CLR));  // open: Qn, preset, en
  D_Flip_Flop pw_2 (.clk(CLK), .D(SOUT_1), .Q(PW2), .reset(CLR));  // open: Qn, preset, en
  and and_1 (and_1_out, PW1, not_1_out);
  not not_1 (not_1_out, nPW1);
  not not_2 (not_2_out, nPW1);
  and and_2 (and_2_out, not_2_out, PW2);
  or or_5 (or_5_out, demultiplexer_4_out0, nPW2);
  Demultiplexer #(.disabled(0)) demultiplexer_4 (
    .out0(demultiplexer_4_out0), .out1(demultiplexer_4_out1), .in(or_5_out), .sel(PRINTYEAR));  // open: en
  or or_6 (PW, and_1_out, and_2_out);
  or or_7 (or_7_out, demultiplexer_4_out1, demultiplexer_5_out0);
  D_Flip_Flop END (.clk(CLK), .D(or_7_out), .Q(END_q), .reset(CLR));  // open: Qn, preset, en
  Demultiplexer #(.disabled(0)) demultiplexer_5 (
    .out0(demultiplexer_5_out0), .out1(demultiplexer_5_out1), .in(END_q), .sel(start));  // open: en

  // Other names for the same wires on the sheet: PRINT2 = nPW1; PRINT3 = nPW2; PD = PRINTDAY; PM = PRINTMONTH;
  //   PY = PRINTYEAR; s0 = SOUT_0; s1 = SOUT_1

  // Notes on the sheet:
  //   PRINTER
endmodule

module Loader (
  input  CLK,
  input  CLR,
  input  START,
  output END,
  output L0,
  output L1,
  output L2,
  output L3,
  output L4,
  output L5
);

  wire demultiplexer_1_out0, demultiplexer_2_out0, demultiplexer_2_out1, IDLE_q, L0_t, L1_t, L2_t, L3_t,
       L4_t, L5_t, not_1_out, not_2_out, not_3_out, not_4_out, not_5_out, not_6_out, or_1_out, or_2_out,
       STOP5;

  or or_1 (or_1_out, demultiplexer_1_out0, demultiplexer_2_out1);
  D_Flip_Flop IDLE (.clk(CLK), .D(or_1_out), .Q(IDLE_q), .preset(CLR));  // open: Qn, en, reset
  Demultiplexer #(.disabled(0)) demultiplexer_1 (
    .out0(demultiplexer_1_out0), .out1(L0_t), .in(IDLE_q), .sel(START));  // open: en
  D_Flip_Flop D0 (.clk(CLK), .D(L0_t), .Q(L1_t), .reset(CLR));  // open: Qn, preset, en
  D_Flip_Flop D1 (.clk(CLK), .D(L1_t), .Q(L2_t), .reset(CLR));  // open: Qn, preset, en
  D_Flip_Flop D2 (.clk(CLK), .D(L2_t), .Q(L3_t), .reset(CLR));  // open: Qn, preset, en
  D_Flip_Flop D3 (.clk(CLK), .D(L3_t), .Q(L4_t), .reset(CLR));  // open: Qn, preset, en
  D_Flip_Flop D4 (.clk(CLK), .D(L4_t), .Q(L5_t), .reset(CLR));  // open: Qn, preset, en
  D_Flip_Flop D5 (.clk(CLK), .D(L5_t), .Q(STOP5), .reset(CLR));  // open: Qn, preset, en
  or or_2 (or_2_out, demultiplexer_2_out0, STOP5);
  Demultiplexer #(.disabled(0)) demultiplexer_2 (
    .out0(demultiplexer_2_out0), .out1(demultiplexer_2_out1), .in(END), .sel(START));  // open: en
  D_Flip_Flop u_END (.clk(CLK), .D(or_2_out), .Q(END), .reset(CLR));  // open: Qn, preset, en
  not not_1 (not_1_out, L1_t);
  not not_2 (not_2_out, L2_t);
  not not_3 (not_3_out, L3_t);
  not not_4 (not_4_out, L4_t);
  not not_5 (not_5_out, L5_t);
  not not_6 (not_6_out, STOP5);
  and and_1 (L0, L0_t, not_1_out);
  and and_2 (L1, L1_t, not_2_out);
  and and_3 (L2, L2_t, not_3_out);
  and and_4 (L3, L3_t, not_4_out);
  and and_5 (L4, L4_t, not_5_out);
  and and_6 (L5, L5_t, not_6_out);

  // Other names for the same wires on the sheet: STOP0 = L1_t; STOP1 = L2_t; STOP2 = L3_t; STOP3 = L4_t; STOP4 = L5_t
endmodule
